# Fritzing sketch AQUI_PCB_V2 (saved by Fritzing 0.9.9b)
circuit board: 14.1cm x 7.7cm
breadboards: 1

parts:
  + = Screw terminal - 2 pins [package=THT]
  -_+_SD_Card = MicroSD Card Module
  S1 = Screw terminal - 2 pins [package=THT]
  S2 = Screw terminal - 2 pins [package=THT]
  S3 = Screw terminal - 2 pins [package=THT]
  S4 = Screw terminal - 2 pins [package=THT]
  S5 = Screw terminal - 2 pins [package=THT]
  S6 = Screw terminal - 2 pins [package=THT]
  Reset = Screw terminal - 2 pins [package=THT]
  -5V+ = Screw terminal - 2 pins [package=THT]
  GND = male pin header, 5 pins [form="♂ (male)"]
  3_3V = male pin header, 5 pins [form="♂ (male)"]
  5V = male pin header, 5 pins [form="♂ (male)"]
  R1 = Resistor [tolerance=±5% power=0.25 resistance=10k package=THT]
  R2 = Resistor [tolerance=±5% power=0.25 resistance=10k package=THT]
  R3 = Resistor [tolerance=±5% power=0.25 resistance=10k package=THT]
  R4 = Resistor [tolerance=±5% power=0.25 resistance=10k package=THT]
  R5 = Resistor [tolerance=±5% power=0.25 resistance=10k package=THT]
  R6 = Resistor [tolerance=±5% power=0.25 resistance=10k package=THT]
  R11 = Resistor [tolerance=±5% power=0.25 resistance=10k package=THT]
  P1_P2 = Screw terminal - 2 pins [package=THT]
  P1_P2_2 = male pin header, 2 pins [form="♂ (male)"]
  R8 = Resistor [tolerance=±5% power=0.25 resistance=10k package=THT]
  R7 = Resistor [tolerance=±5% power=0.25 resistance=10k package=THT]
  S8 = Screw terminal - 2 pins [package=THT]
  S7 = Screw terminal - 2 pins [package=THT]
  R12 = Resistor [tolerance=±5% power=0.25 resistance=4.7k package=THT]
  I²C1 = female pin header, 4 pins [form="♀ (female)"]
  -_+ = male pin header, 2 pins [form="♂ (male)"]
  I²C1_2 = female pin header, 4 pins [form="♀ (female)"]
  I²C2 = female pin header, 4 pins [form="♀ (female)"]
  I²C3 = female pin header, 4 pins [form="♀ (female)"]
  I²C4 = female pin header, 4 pins [form="♀ (female)"]
  T2 = LM35 Temperature Sensor [package="TO92 [THT]"]
  T1_- = Screw terminal - 2 pins [package=THT]
  I²C5 = female pin header, 4 pins [form="♀ (female)"]
  Buzzer_- = Piezo Speaker - PC Mount [part_number=COM-07950]
  ESP32 = ESP32-38PinWide [part_number=ESP32]
  R9 = Resistor [tolerance=±5% power=0.25 resistance=10k package=THT]
  S9 = Screw terminal - 2 pins [package=THT]
  R10 = Resistor [tolerance=±5% power=0.25 resistance=10k package=THT]
  S10 = Screw terminal - 2 pins [package=THT]
  T3 = LM35 Temperature Sensor [package="TO92 [THT]"]
  C2 = Electrolytic Capacitor [capacitance=47µF voltage=35V package="100 mil [THT, electrolytic]"]
  C1 = Electrolytic Capacitor [capacitance=47µF voltage=35V package="100 mil [THT, electrolytic]"]

nets:
  5V: +.pin1, -_+_SD_Card.VCC, -5V+.pin2, 5V.pin1, 5V.pin2, 5V.pin3, 5V.pin4, 5V.pin5, R12.Pin_1, I²C1.pin1, -_+.pin2, I²C1_2.pin1, I²C2.pin1, I²C3.pin1, I²C4.pin1, T2.+Vs, I²C5.pin1, ESP32.VIN, T3.+Vs, C2.+, C1.+
  GND: -_+_SD_Card.GND, -5V+.pin1, GND.pin1, GND.pin2, GND.pin3, GND.pin4, GND.pin5, R1.Pin_1, R2.Pin_1, R3.Pin_1, R4.Pin_1, R5.Pin_1, R6.Pin_1, R11.Pin_1, R8.Pin_1, R7.Pin_1, I²C1.pin4, -_+.pin1, I²C1_2.pin4, I²C2.pin4, I²C3.pin4, I²C4.pin4, T2.GND, T1_-.pin1, I²C5.pin4, Buzzer_-.GND, ESP32.GND, R9.Pin_1, R10.Pin_1, T3.GND, C2.-, C1.-
  IO19: -_+_SD_Card.MISO, ESP32.GPIO19
  IO23: -_+_SD_Card.MOSI, ESP32.GPIO23
  IO18: -_+_SD_Card.SCK, ESP32.GPIO18
  IO5: -_+_SD_Card.CS, ESP32.GPIO5
  IO34: S1.pin1, R1.Pin_0, ESP32.GPIO34
  3.3V: S1.pin2, S2.pin2, S3.pin2, S4.pin2, S5.pin2, S6.pin2, Reset.pin2, 3_3V.pin1, 3_3V.pin2, 3_3V.pin3, 3_3V.pin4, 3_3V.pin5, S8.pin2, S7.pin2, ESP32.3.3, S9.pin2, S10.pin2
  IO35: S2.pin1, R2.Pin_0, ESP32.GPIO35
  IO32: S3.pin1, R3.Pin_0, ESP32.GPIO32
  IO33: S4.pin1, R4.Pin_0, ESP32.GPIO33
  IO25: S5.pin1, R5.Pin_0, ESP32.GPIO25
  IO26: S6.pin1, R6.Pin_0, ESP32.GPIO26
  IO17: Reset.pin1, R11.Pin_0, ESP32.GPIO17
  IO2: P1_P2.pin1, P1_P2_2.pin1, ESP32.GPIO2
  IO16: P1_P2.pin2, P1_P2_2.pin2, ESP32.GPIO16
  IO14: R8.Pin_0, S8.pin1, ESP32.GPIO14
  IO27: R7.Pin_0, S7.pin1, ESP32.GPIO27
  IO4: R12.Pin_0, T1_-.pin2, ESP32.GPIO4
  SCL: I²C1.pin2, I²C1_2.pin2, I²C2.pin2, I²C3.pin2, I²C4.pin2, I²C5.pin2, ESP32.GPIO22
  SDA: I²C1.pin3, I²C1_2.pin3, I²C2.pin3, I²C3.pin3, I²C4.pin3, I²C5.pin3, ESP32.GPIO21
  IO39: T2.Vout, ESP32.GPIO39
  IO12: Buzzer_-.VCC, ESP32.GPIO12
  IO36: ESP32.GPIO36, T3.Vout
  IO13: ESP32.GPIO13, R9.Pin_0, S9.pin1
  IO15: ESP32.GPIO15, R10.Pin_0, S10.pin1

notes:
  AQUI
  Controller
  Board V2.0
  Designed by Felix Scholzen
  3.3V
  GND
  VIN
  ESP32
  USB
  I²C Bus
  + SDA SCL -
  Schwimmerschalter
  LM35 Temperatur Sensoren
  Pumpen Outputs
  Reset Button
  DS18B20 Temperatur Sensor
  Strom Ouputs
  Buzzer
  Power In
  ESP32 Node MCU
  MicroSD Card
  2

custom parts:
  Piezo Speaker - PC Mount: This is a small 12mm round speaker that operates around the audible 2kHz range. You can use these speakers to create simple music or user interfaces. Each speaker is PTH solderable and requires an operating voltage of 3.5-5V with a mean current of 35mA max. These speakers also have a typical sound output of 95 dBA and a coil resistance of 42 ±6.3 ohms.
  ESP32-38PinWide: Generic 38-Pin ESP32 with wide format (only access to one side of pins on a breadboard) based on Stephen Lilley's HiLetgo ESP-WROOM-32 ESP32 ESP-32S Development Board.
